# Fritzing sketch Circuit_Layout (saved by Fritzing 0.9.3b)

parts:
  Part1 = Arduino Ethernet Shield (Rev3)
  Part2 = Arduino Uno (Rev3) - ICSP  # not connected
  LED1 = smd LED [color="Blue (470nm)" package="0603 [SMD]"]
  U1 = POT [package=pot_mammoth]
  Part3 = InvenSense MPU6050
  M2 = ESC
  920KV_Motor2 = DJI 920 KV Motor
  U2 = LIPO-1000mAh [package=lipo-1000]

nets:
  N1: Part1.PWM_D9, M2.DATA
  N2: Part1.SPI/D13, LED1.anode
  GND: Part1.GND, LED1.cathode, U1.S, Part3.GND, U2.-
  N3: Part1.A0, U1.A
  N4: Part1.A4/SDA, Part3.SDA
  N5: Part1.A5/SCL, Part3.SCL
  5V: Part1.5V, U1.E, Part3.VCC
  N6: M2.U, 920KV_Motor2.u
  N7: M2.V, 920KV_Motor2.v
  N8: M2.W, 920KV_Motor2.w

notes:
  + and - are INTENTIONALLY left disconnected. ----->
  Arduino UNO w/ ethernet shield
  3S Lipo Battery

custom parts:
  DJI 920 KV Motor: DJI Brushless Outrunner 2212/920K Motor F330-550

// code stored in the sketch: MecE668.ino

